// Logisim project BancDeRegistres.circ as structural Verilog: 1 circuit, main circuit BancRegistre
// R3
module BancRegistre (
  input  Reset,
  input  [2:0] RegA,
  input  [31:0] DataIn,
  input  [2:0] RegDest,
  input  [2:0] RegB,
  input  Clk,
  output [31:0] R0,
  output [31:0] R1,
  output [31:0] AOut,
  output [31:0] R2,
  output [31:0] R3,
  output [31:0] R4,
  output [31:0] BOut,
  output [31:0] R5,
  output [31:0] R6,
  output [31:0] R7
);

  wire [31:0] R0_t, R1_t, R2_t, R3_t, R4_t, R5_t, R6_t, R7_t;

  Demultiplexer #(.enable("false"), .select(3), .width(32)) demultiplexer_1 (
    .out0(R0), .out1(R1), .out2(R2), .out3(R3), .out4(R4), .out5(R5), .out6(R6), .out7(R7), .in(DataIn),
    .sel(RegDest));
  Multiplexer #(.enable("false"), .select(3), .width(32)) multiplexer_1 (
    .in0(R0_t), .in1(R1_t), .in2(R2_t), .in3(R3_t), .in4(R4_t), .in5(R5_t), .in6(R6_t), .in7(R7_t),
    .out(AOut), .sel(RegA));
  Multiplexer #(.enable("false"), .select(3), .width(32)) multiplexer_2 (
    .in0(R0_t), .in1(R1_t), .in2(R2_t), .in3(R3_t), .in4(R4_t), .in5(R5_t), .in6(R6_t), .in7(R7_t),
    .out(BOut), .sel(RegB));
endmodule
