// Logisim project Ctl_Data_Processing.circ as structural Verilog: 2 circuits, main circuit Data_Processing
module Data_Processing (
  input  Enable,
  input  [15:0] Instruction,
  output [2:0] Rd,
  output [2:0] Rn,
  output [2:0] Rm,
  output [3:0] ALU_Opcode,
  output [3:0] Flags_Update_Mask
);

  wire [2:0] bitselector_1_out, bitselector_2_out, undriven;
  wire [3:0] bitselector_4_out, table_de_verite_1_flags;
  wire [5:0] bitselector_3_out;

  BitSelector #(.group(3), .width(16)) bitselector_1 (.in(Instruction), .out(bitselector_1_out), .sel(undriven));
  BitSelector #(.group(3), .width(16)) bitselector_2 (.in(Instruction), .out(bitselector_2_out));  // open: sel
  BitSelector #(.group(6), .width(16)) bitselector_3 (.in(Instruction), .out(bitselector_3_out), .sel(2'b01));
  BitSelector #(.group(4), .width(6)) bitselector_4 (.in(bitselector_3_out), .out(bitselector_4_out), .sel(1'b0));
  Multiplexer #(.enable("false"), .width(3)) multiplexer_1 (
    .in0(3'b000), .in1(bitselector_1_out), .out(Rd), .sel(Enable));
  Multiplexer #(.enable("false"), .width(3)) multiplexer_2 (.in0(3'b000), .in1(undriven), .out(Rn), .sel(Enable));
  Multiplexer #(.enable("false"), .width(3)) multiplexer_3 (
    .in0(3'b000), .in1(bitselector_2_out), .out(Rm), .sel(Enable));
  Multiplexer #(.enable("false"), .width(4)) multiplexer_4 (
    .in0(4'b0000), .in1(bitselector_4_out), .out(ALU_Opcode), .sel(Enable));
  Table_de_Verite table_de_verite_1 (.Codop(bitselector_4_out), .Flags(table_de_verite_1_flags));
  Multiplexer #(.enable("false"), .width(4)) multiplexer_5 (
    .in0(4'b0000), .in1(table_de_verite_1_flags), .out(Flags_Update_Mask), .sel(Enable));

  // Notes on the sheet:
  //   Note 2: RSB instruction has Rn as 1st operand.
  //   MUL instruction has Rn as 1st operand and Rdm as 2nd operand
  //   For simplification purposes, Rm is used for 1st operand both here and in the ALU.
  //   Note: instructions that does not save the result will still have the second operand as the destination register, the ALU will copy the second register to the destination register
  //   Pull output low on Enable = 0
endmodule

module Table_de_Verite (
  input  [3:0] Codop,
  output [3:0] Flags
);

  wire and_1_out, and_2_out, and_3_out, and_4_out, and_5_out, and_6_out, not_1_out, not_2_out, not_3_out,
       not_4_out;

  not not_1 (not_1_out, Codop[3]);
  not not_2 (not_2_out, Codop[2]);
  not not_3 (not_3_out, Codop[1]);
  not not_4 (not_4_out, Codop[0]);
  and and_1 (and_1_out, not_2_out, Codop[1]);
  and and_2 (and_2_out, not_1_out, Codop[2], not_3_out);
  and and_3 (and_3_out, not_1_out, Codop[2], not_4_out);
  and and_4 (and_4_out, Codop[2], not_3_out, not_4_out);
  and and_5 (and_5_out, not_1_out, Codop[2], Codop[1]);
  and and_6 (and_6_out, Codop[3], not_2_out, Codop[1]);
  or or_1 (Flags[1], and_1_out, and_2_out, and_3_out, and_4_out);
  or or_2 (Flags[0], and_5_out, and_6_out);

  assign Flags[3:2] = 2'b11;
endmodule
