// Logisim project Ctl_SP_Address.circ as structural Verilog: 1 circuit, main circuit SP_Address
module SP_Address (
  input  Enable,
  input  [15:0] Instruction,
  input  [31:0] Stack_Pointer,
  output Write_Enable,
  output [31:0] New_Stack_Pointer
);

  wire bitselector_2_out;
  wire [7:0] bitselector_1_out;
  wire [31:0] A, adder_1_out, multiplexer_1_out, subtractor_1_out;

  assign A = {{24{1'b0}}, bitselector_1_out};  // Bit_Extender bit_extender_1
  BitSelector #(.group(8), .width(16)) bitselector_1 (.in(Instruction), .out(bitselector_1_out), .sel(1'b0));
  BitSelector #(.width(16)) bitselector_2 (.in(Instruction), .out(bitselector_2_out), .sel(4'b0111));
  Adder #(.width(32)) adder_1 (.a(A), .b(Stack_Pointer), .out(adder_1_out));  // open: cin, cout
  Subtractor #(.width(32)) subtractor_1 (.a(A), .b(Stack_Pointer), .out(subtractor_1_out));  // open: bin, bout
  Multiplexer #(.enable("false"), .width(32)) multiplexer_1 (
    .in0(adder_1_out), .in1(subtractor_1_out), .out(multiplexer_1_out), .sel(bitselector_2_out));
  assign New_Stack_Pointer = Enable ? multiplexer_1_out : 32'bz;  // Controlled_Buffer controlled_buffer_1

  assign Write_Enable = Enable;

  // Other names for the same wires on the sheet: B[31:0] = Stack_Pointer

  // Notes on the sheet:
  //   Pull output low on Enable = 0
endmodule
