// Logisim project Ctl_Shift_Add_Sub_Mov.circ as structural Verilog: 11 circuits, main circuit table_de_verite
module Shift_Add_Sub_Mov (
  input  Enable,
  input  [15:0] Instruction,
  output [3:0] Flags_Update_Mask,
  output Carry,
  output Imm32_Enable,
  output [2:0] Rd,
  output [2:0] Rn,
  output [2:0] Rm,
  output [4:0] Imm5,
  output [31:0] Imm32,
  output [3:0] ALU_Opcode
);

  wire carry_table_1_out_2, im32_enable_table_1_im32, imm5_e_1_enable;
  wire [2:0] rm_rn_rd_1_rd, rm_rn_rd_1_rm, rm_rn_rd_1_rn;
  wire [3:0] flags_table_1_flags, table_de_verite_1_out_2;
  wire [4:0] bitselector_3_out, bitselector_4_out, multiplexer_1_out;
  wire [5:0] bitselector_2_out;
  wire [8:0] bitselector_1_out;
  wire [31:0] imm32enable_1_sortie;

  BitSelector #(.group(9), .width(16)) bitselector_1 (.in(Instruction), .out(bitselector_1_out), .sel(1'b1));
  BitSelector #(.group(6), .width(16)) bitselector_2 (.in(Instruction), .out(bitselector_2_out), .sel(2'b01));
  BitSelector #(.group(5), .width(9)) bitselector_3 (.in(bitselector_1_out), .out(bitselector_3_out), .sel(1'b0));
  BitSelector #(.group(5), .width(6)) bitselector_4 (.in(bitselector_2_out), .out(bitselector_4_out), .sel(1'b0));
  imm5_e imm5_e_1 (.codop(bitselector_3_out), .enable(imm5_e_1_enable));
  Multiplexer #(.enable("false"), .width(5)) multiplexer_1 (
    .in0({5{1'b0}}), .in1(bitselector_4_out), .out(multiplexer_1_out), .sel(imm5_e_1_enable));
  Rm_Rn_Rd rm_rn_rd_1 (.instruction(Instruction), .Rd(rm_rn_rd_1_rd), .Rn(rm_rn_rd_1_rn), .Rm(rm_rn_rd_1_rm));
  Imm32Enable imm32enable_1 (.instructions(Instruction), .sortie(imm32enable_1_sortie));
  Multiplexer #(.enable("false"), .width(4)) multiplexer_2 (
    .in0(4'b0000), .in1(flags_table_1_flags), .out(Flags_Update_Mask), .sel(Enable));
  Flags_table flags_table_1 (.codop(bitselector_3_out), .flags(flags_table_1_flags));
  Multiplexer #(.enable("false")) multiplexer_3 (.in0(Enable), .in1(carry_table_1_out_2), .out(Carry), .sel(Enable));
  carry_table carry_table_1 (.in_1(bitselector_3_out), .out_2(carry_table_1_out_2));
  Multiplexer #(.enable("false")) multiplexer_4 (
    .in0(1'b0), .in1(im32_enable_table_1_im32), .out(Imm32_Enable), .sel(Enable));
  Im32_Enable_table im32_enable_table_1 (.codop(bitselector_3_out), .im32(im32_enable_table_1_im32));
  Multiplexer #(.enable("false"), .width(3)) multiplexer_5 (.in0(3'b000), .in1(rm_rn_rd_1_rd), .out(Rd), .sel(Enable));
  Multiplexer #(.enable("false"), .width(3)) multiplexer_6 (.in0(3'b000), .in1(rm_rn_rd_1_rn), .out(Rn), .sel(Enable));
  Multiplexer #(.enable("false"), .width(3)) multiplexer_7 (.in0(3'b000), .in1(rm_rn_rd_1_rm), .out(Rm), .sel(Enable));
  Multiplexer #(.enable("false"), .width(5)) multiplexer_8 (
    .in0({5{1'b0}}), .in1(multiplexer_1_out), .out(Imm5), .sel(Enable));
  Multiplexer #(.enable("false"), .width(32)) multiplexer_9 (
    .in0({32{1'b0}}), .in1(imm32enable_1_sortie), .out(Imm32), .sel(Enable));
  Multiplexer #(.enable("false"), .width(4)) multiplexer_10 (
    .in0(4'b0000), .in1(table_de_verite_1_out_2), .out(ALU_Opcode), .sel(Enable));
  table_de_verite table_de_verite_1 (.in_1(bitselector_3_out), .out_2(table_de_verite_1_out_2));

  // Other names for the same wires on the sheet: E = Enable

  // Notes on the sheet:
  //   Note: ALU uses Rn register for shifts. Use Rn instead of Rm for shifts (immediate) here too
  //   Note 3: Imm32_Enable forces the use of the immediate for Rm register
  //   Note 2: MOV uses RSB ALU opcode with Imm8 reversed so that it is copied to output register
  //   Pull output low on Enable = 0
  //   Enable carry for SUB since it is reversed in ALU
  //   ALU will use Imm32 instead of Rm
  //   only ADD and SUB use Rm
endmodule

module table_de_verite (
  input  [4:0] in_1,
  output [3:0] out_2
);

  wire and_2_out, and_3_out, and_4_out, and_5_out, and_6_out, and_7_out, not_1_out, not_2_out, not_3_out,
       not_4_out;

  not not_1 (not_1_out, in_1[4]);
  not not_2 (not_2_out, in_1[3]);
  not not_3 (not_3_out, in_1[2]);
  not not_4 (not_4_out, in_1[0]);
  and and_1 (out_2[3], in_1[4], not_2_out);
  and and_2 (and_2_out, not_1_out, not_2_out);
  and and_3 (and_3_out, in_1[2], in_1[0]);
  and and_4 (and_4_out, in_1[4], in_1[2]);
  and and_5 (and_5_out, not_1_out, not_2_out, in_1[2]);
  and and_6 (and_6_out, not_1_out, in_1[2], not_4_out);
  and and_7 (and_7_out, in_1[4], not_3_out);
  or or_1 (out_2[1], and_2_out, and_3_out, and_4_out);
  or or_2 (out_2[0], and_5_out, and_6_out, and_7_out);

  assign out_2[2] = in_1[3];
endmodule

module carry_table (
  input  [4:0] in_1,
  output out_2
);

  wire and_1_out, not_1_out, not_2_out, not_3_out;

  not not_1 (not_1_out, in_1[3]);
  not not_2 (not_2_out, in_1[2]);
  not not_3 (not_3_out, in_1[1]);
  and and_1 (and_1_out, not_1_out, not_3_out);
  or or_1 (out_2, and_1_out, not_2_out, in_1[0], in_1[4]);
endmodule

module Im32_Enable_table (
  input  [4:0] codop,
  output im32
);

  wire and_1_out;

  and and_1 (and_1_out, codop[3], codop[2], codop[1]);
  or or_1 (im32, and_1_out, codop[4]);
endmodule

module Flags_table (
  input  [4:0] codop,
  output [3:0] flags
);

  wire and_1_out, and_2_out, and_3_out, not_1_out;

  not not_1 (not_1_out, codop[4]);
  or or_1 (flags[1], not_1_out, codop[2], codop[3]);
  and and_1 (and_1_out, codop[3], codop[2]);
  and and_2 (and_2_out, codop[4], codop[2]);
  and and_3 (and_3_out, codop[4], codop[3]);
  or or_2 (flags[0], and_1_out, and_2_out, and_3_out);

  assign flags[3:2] = 2'b11;
endmodule

module Imm32Enable (
  input  [15:0] instructions,
  output [31:0] sortie
);

  wire bitselector_1_out, mov_enable_1_enable;
  wire [2:0] bitselector_5_out, bitselector_6_out;
  wire [7:0] bitselector_3_out, bitselector_4_out;
  wire [8:0] bitselector_2_out;
  wire [31:0] A, B, multiplexer_1_out, negator_1_out;

  BitSelector #(.width(16)) bitselector_1 (.in(instructions), .out(bitselector_1_out), .sel(4'b1101));
  BitSelector #(.group(9), .width(16)) bitselector_2 (.in(instructions), .out(bitselector_2_out), .sel(1'b0));
  BitSelector #(.group(8), .width(16)) bitselector_3 (.in(instructions), .out(bitselector_3_out), .sel(1'b0));
  BitSelector #(.group(8), .width(16)) bitselector_4 (.in(instructions), .out(bitselector_4_out), .sel(1'b1));
  BitSelector #(.group(3)) bitselector_5 (.in(bitselector_4_out), .out(bitselector_5_out), .sel(2'b01));
  assign A = {{29{1'b0}}, bitselector_6_out};  // Bit_Extender bit_extender_1
  BitSelector #(.group(3), .width(9)) bitselector_6 (.in(bitselector_2_out), .out(bitselector_6_out), .sel(2'b10));
  assign B = {{24{1'b0}}, bitselector_3_out};  // Bit_Extender bit_extender_2
  Multiplexer #(.enable("false"), .width(32)) multiplexer_1 (
    .in0(A), .in1(B), .out(multiplexer_1_out), .sel(bitselector_1_out));
  mov_enable mov_enable_1 (.codop(bitselector_5_out), .enable(mov_enable_1_enable));
  Negator #(.width(32)) negator_1 (.in(multiplexer_1_out), .out(negator_1_out));
  Multiplexer #(.enable("false"), .width(32)) multiplexer_2 (
    .in0(multiplexer_1_out), .in1(negator_1_out), .out(sortie), .sel(mov_enable_1_enable));
endmodule

module Rm_Rn_Rd (
  input  [15:0] instruction,
  output [2:0] Rd,
  output [2:0] Rn,
  output [2:0] Rm
);

  wire bitselector_4_out, rmenable_1_enable;
  wire [2:0] bitselector_1_out, bitselector_2_out, bitselector_5_out, bitselector_7_out;
  wire [3:0] bitselector_8_out;
  wire [7:0] bitselector_6_out;
  wire [9:0] bitselector_3_out;

  BitSelector #(.group(3), .width(16)) bitselector_1 (.in(instruction), .out(bitselector_1_out), .sel(3'b001));
  BitSelector #(.group(3), .width(16)) bitselector_2 (.in(instruction), .out(bitselector_2_out), .sel(3'b010));
  BitSelector #(.group(10), .width(16)) bitselector_3 (.in(instruction), .out(bitselector_3_out), .sel(1'b1));
  BitSelector #(.width(16)) bitselector_4 (.in(instruction), .out(bitselector_4_out), .sel(4'b1101));
  BitSelector #(.group(3), .width(16)) bitselector_5 (.in(instruction), .out(bitselector_5_out), .sel(3'b000));
  BitSelector #(.group(8), .width(16)) bitselector_6 (.in(instruction), .out(bitselector_6_out), .sel(1'b1));
  BitSelector #(.group(3)) bitselector_7 (.in(bitselector_6_out), .out(bitselector_7_out), .sel(2'b00));
  BitSelector #(.group(4), .width(10)) bitselector_8 (.in(bitselector_3_out), .out(bitselector_8_out), .sel(2'b00));
  Multiplexer #(.enable("false"), .width(3)) multiplexer_1 (
    .in0(bitselector_5_out), .in1(bitselector_7_out), .out(Rd), .sel(bitselector_4_out));
  Multiplexer #(.enable("false"), .width(3)) multiplexer_2 (
    .in0(bitselector_1_out), .in1(3'b000), .out(Rn), .sel(bitselector_4_out));
  Multiplexer #(.enable("false"), .width(3)) multiplexer_3 (
    .in0(3'b000), .in1(bitselector_2_out), .out(Rm), .sel(rmenable_1_enable));
  RmEnable rmenable_1 (.op1310(bitselector_8_out), .enable(rmenable_1_enable));
endmodule

module imm5_e (
  input  [4:0] codop,
  output enable
);

  wire and_1_out, and_2_out, not_1_out, not_2_out, not_3_out;

  not not_1 (not_1_out, codop[4]);
  not not_2 (not_2_out, codop[3]);
  not not_3 (not_3_out, codop[2]);
  and and_1 (and_1_out, not_1_out, not_2_out);
  and and_2 (and_2_out, not_1_out, not_3_out);
  or or_1 (enable, and_1_out, and_2_out);
endmodule

module cmp_enable (
  input  [2:0] codop,
  output enable
);

  wire not_1_out;

  not not_1 (not_1_out, codop[1]);
  and and_1 (enable, codop[2], not_1_out, codop[0]);
endmodule

module RmEnable (
  input  [3:0] op1310,
  output enable
);

  wire not_1_out, not_2_out;

  not not_1 (not_1_out, op1310[3]);
  not not_2 (not_2_out, op1310[0]);
  and and_1 (enable, not_1_out, op1310[2], op1310[1], not_2_out);
endmodule

module mov_enable (
  input  [2:0] codop,
  output enable
);

  wire not_1_out, not_2_out;

  not not_1 (not_1_out, codop[1]);
  not not_2 (not_2_out, codop[0]);
  and and_1 (enable, codop[2], not_1_out, not_2_out);
endmodule
